# Fritzing sketch IR_Clock (saved by Fritzing 0.9.2b)
breadboards: 1

parts:
  U1 = TEMPERATURE-SENSOR [package=to-92]
  RHT1 = Humidity and Temperature Sensor RHT03
  元件1 = Barometric Pressure Sensor - BMP085 Breakout
  元件2 = Real Time Clock Module - DS1307 RTC Breakout Board
  IR1 = TSOP312.., 314.. [package=THT]
  元件4 = Tri-Axis Gyro Breakout - L3G4200D
  元件5 = Arduino Uno (Rev3)
  LCD1 = LCD screen
  R2 = Trimmer Potentiometer [maximum_resistance=10kΩ package=THT]
  R3 = Resistor [tolerance=±5% resistance=220 package=THT]
  C2 = Ceramic Capacitor [capacitance=100nF package="100 mil [THT, multilayer]"]  # not connected
  SPKR1 = Loudspeaker
  R6 = Resistor [tolerance=±5% resistance=220 package=THT]
  R7 = Resistor [tolerance=±5% resistance=220 package=THT]

nets:
  GND: U1.GND, RHT1.GND_1, 元件1.GND, 元件2.GND, IR1.GND, 元件4.GND, 元件5.GND, LCD1.VSS, LCD1.R/W, R2.leg2, R3.Pin_0
  N1: U1.ADJ, 元件5.D9_PWM, R6.Pin_1
  VCC: U1.VCC, RHT1.Vcc, 元件1.VCC, 元件2.5V, IR1.Vs, 元件4.VCC, 元件5.5V, LCD1.LED+, R2.leg1, R6.Pin_0, R7.Pin_1
  N2: RHT1.Data-signal, 元件5.A0, R7.Pin_0
  N3: 元件1.SCL, 元件2.SCL, 元件5.A5/SCL
  N4: 元件1.SDA, 元件2.SDA, 元件5.A4/SDA
  N5: IR1.Data, 元件5.D8
  N6: 元件4.SCL, 元件5.D13/SCK
  N7: 元件4.SDA, 元件5.D11_PWM/MOSI
  N8: 元件4.SDO, 元件5.D12/MISO
  N9: 元件4.CS, 元件5.D10_PWM/SS
  N10: 元件4.INT2, SPKR1.pin1
  N11: 元件4.INT1, SPKR1.pin2
  N12: 元件5.D2, LCD1.RS
  N13: 元件5.D3_PWM, LCD1.E
  N14: 元件5.D4, LCD1.DB4
  N15: 元件5.D5_PWM, LCD1.DB5
  N16: 元件5.D6_PWM, LCD1.DB6
  N17: 元件5.D7, LCD1.DB7
  N18: LCD1.V0, R2.wiper
  N19: LCD1.LED-, R3.Pin_1
